// Logisim project pong_cpu.circ as structural Verilog
module FullAdder (
  input  A,
  input  B,
  input  Cin,
  output SUM,
  output COUT
);

  wire and_1_out, and_2_out, xor_1_out;

  xor xor_1 (xor_1_out, A, B);
  and and_1 (and_1_out, B, A);
  xor xor_2 (SUM, xor_1_out, Cin);
  and and_2 (and_2_out, Cin, xor_1_out);
  or or_1 (COUT, and_2_out, and_1_out);
endmodule

module FourBitAdder (
  input  B3,
  input  A3,
  input  A2,
  input  B1,
  input  A1,
  input  B2,
  input  B0,
  input  A0,
  input  C0,
  output S0,
  output S2,
  output S1,
  output COUT,
  output S3
);

  wire fulladder_2_cout, fulladder_3_cout, fulladder_4_cout;

  FullAdder fulladder_1 (.A(A3), .B(B3), .Cin(fulladder_2_cout), .SUM(S3), .COUT(COUT));
  FullAdder fulladder_2 (.A(A2), .B(B2), .Cin(fulladder_3_cout), .SUM(S2), .COUT(fulladder_2_cout));
  FullAdder fulladder_3 (.A(A1), .B(B1), .Cin(fulladder_4_cout), .SUM(S1), .COUT(fulladder_3_cout));
  FullAdder fulladder_4 (.A(A0), .B(B0), .Cin(C0), .SUM(S0), .COUT(fulladder_4_cout));
endmodule

module AND4 (
  input  [3:0] A,
  input  [3:0] B,
  output [3:0] R
);

  assign R = A & B;  // AND_Gate and_1, 4 bits wide
endmodule

module OR4 (
  input  [3:0] A,
  input  [3:0] B,
  output [3:0] R
);

  assign R = A | B;  // OR_Gate or_1, 4 bits wide
endmodule

module XOR4 (
  input  [3:0] A,
  input  [3:0] B,
  output [3:0] R
);

  assign R = A ^ B;  // XOR_Gate xor_1, 4 bits wide
endmodule

module ArithmeticUnit (
  input  [3:0] B,
  input  [3:0] A,
  input  SUB,
  output [3:0] AUResult,
  output COUT
);

  wire [3:0] bit_extender_1_out, xor4_1_r;

  assign bit_extender_1_out = {{3{SUB}}, SUB};  // Bit_Extender bit_extender_1
  XOR4 xor4_1 (.A(bit_extender_1_out), .B(B), .R(xor4_1_r));
  FourBitAdder fourbitadder_1 (
    .B3(xor4_1_r[3]), .A3(A[3]), .A2(A[2]), .B1(xor4_1_r[1]), .A1(A[1]), .B2(xor4_1_r[2]), .B0(xor4_1_r[0]),
    .A0(A[0]), .C0(SUB), .S0(AUResult[0]), .S2(AUResult[2]), .S1(AUResult[1]), .COUT(COUT), .S3(AUResult[3]));
endmodule

module ALU (
  input  [3:0] A,
  input  [3:0] B,
  input  [1:0] OPRATION,
  output AluCout,
  output [3:0] AluResult
);

  wire [3:0] arithmeticunit_1_auresult, lu_1_and_res, lu_1_or_res;

  ArithmeticUnit arithmeticunit_1 (
    .B(B), .A(A), .SUB(OPRATION[0]), .AUResult(arithmeticunit_1_auresult), .COUT(AluCout));
  LU lu_1 (.A(A), .B(B), .AND_RES(lu_1_and_res), .OR_RES(lu_1_or_res));
  Multiplexer #(.select(2), .width(4)) multiplexer_1 (
    .in0(arithmeticunit_1_auresult), .in1(arithmeticunit_1_auresult), .in2(lu_1_and_res), .in3(lu_1_or_res),
    .out(AluResult), .sel(OPRATION));
endmodule

module LU (
  input  [3:0] A,
  input  [3:0] B,
  output [3:0] AND_RES,
  output [3:0] OR_RES
);

  AND4 and4_1 (.A(A), .B(B), .R(AND_RES));
  OR4 or4_1 (.A(A), .B(B), .R(OR_RES));
endmodule

module SRLatch (
  input  R,
  input  S,
  output Q,
  output NotQ
);

  nor nor_1 (Q, R, NotQ);
  nor nor_2 (NotQ, Q, S);
endmodule

module DLatchEN (
  input  D,
  input  EN,
  output Q,
  output NotQ
);

  wire and_1_out, and_2_out, not_1_out;

  not not_1 (not_1_out, D);
  and and_1 (and_1_out, D, EN);
  and and_2 (and_2_out, EN, not_1_out);
  SRLatch srlatch_1 (.R(and_2_out), .S(and_1_out), .Q(Q), .NotQ(NotQ));
endmodule

module DFlipFlop (
  input  D,
  input  CLOCK,
  output Q,
  output NotQ
);

  wire Master_q, not_1_out;

  not not_1 (not_1_out, CLOCK);
  DLatchEN Master (.D(D), .EN(not_1_out), .Q(Master_q));  // open: NotQ
  DLatchEN Slave (.D(Master_q), .EN(CLOCK), .Q(Q), .NotQ(NotQ));
endmodule

module FourBitRegister (
  input  LOAD,
  input  CLOCK,
  input  D3,
  input  D2,
  input  D1,
  input  D0,
  output Q3,
  output Q2,
  output Q1,
  output Q0
);

  wire multiplexer_1_out, multiplexer_2_out, multiplexer_3_out, multiplexer_4_out;

  Multiplexer multiplexer_1 (.in0(Q3), .in1(D3), .out(multiplexer_1_out), .sel(LOAD));
  Multiplexer multiplexer_2 (.in0(Q2), .in1(D2), .out(multiplexer_2_out), .sel(LOAD));
  Multiplexer multiplexer_3 (.in0(Q1), .in1(D1), .out(multiplexer_3_out), .sel(LOAD));
  Multiplexer multiplexer_4 (.in0(Q0), .in1(D0), .out(multiplexer_4_out), .sel(LOAD));
  DFlipFlop DFF3 (.D(multiplexer_1_out), .CLOCK(CLOCK), .Q(Q3));  // open: NotQ
  DFlipFlop DFF2 (.D(multiplexer_2_out), .CLOCK(CLOCK), .Q(Q2));  // open: NotQ
  DFlipFlop DFF1 (.D(multiplexer_3_out), .CLOCK(CLOCK), .Q(Q1));  // open: NotQ
  DFlipFlop DFF0 (.D(multiplexer_4_out), .CLOCK(CLOCK), .Q(Q0));  // open: NotQ
endmodule

module Decoder2to4 (
  input  A1,
  input  A0,
  output Y0,
  output Y1,
  output Y2,
  output Y3
);

  wire not_1_out, not_2_out;

  not not_1 (not_1_out, A0);
  not not_2 (not_2_out, A1);
  and and_1 (Y0, not_1_out, not_2_out);
  and and_2 (Y1, not_2_out, A0);
  and and_3 (Y2, not_1_out, A1);
  and and_4 (Y3, A0, A1);
endmodule

module RegisterFile (
  input  D3,
  input  D2,
  input  D1,
  input  D0,
  input  CLOCK,
  input  [1:0] READ_ADRS_A,
  input  [1:0] READ_ADRS_B,
  input  Decoder_A0,
  input  Decoder_A1,
  output [3:0] READ_A,
  output [3:0] READ_B
);

  wire decoder2to4_1_y0, decoder2to4_1_y1, decoder2to4_1_y2, decoder2to4_1_y3;
  wire [3:0] R0_q0, R1_q0, R2_q0, R3_q0;

  FourBitRegister R0 (
    .LOAD(decoder2to4_1_y0), .CLOCK(CLOCK), .D3(D3), .D2(D2), .D1(D1), .D0(D0), .Q3(R0_q0[3]), .Q2(R0_q0[2]),
    .Q1(R0_q0[1]), .Q0(R0_q0[0]));
  FourBitRegister R1 (
    .LOAD(decoder2to4_1_y1), .CLOCK(CLOCK), .D3(D3), .D2(D2), .D1(D1), .D0(D0), .Q3(R1_q0[3]), .Q2(R1_q0[2]),
    .Q1(R1_q0[1]), .Q0(R1_q0[0]));
  FourBitRegister R2 (
    .LOAD(decoder2to4_1_y2), .CLOCK(CLOCK), .D3(D3), .D2(D2), .D1(D1), .D0(D0), .Q3(R2_q0[3]), .Q2(R2_q0[2]),
    .Q1(R2_q0[1]), .Q0(R2_q0[0]));
  FourBitRegister R3 (
    .LOAD(decoder2to4_1_y3), .CLOCK(CLOCK), .D3(D3), .D2(D2), .D1(D1), .D0(D0), .Q3(R3_q0[3]), .Q2(R3_q0[2]),
    .Q1(R3_q0[1]), .Q0(R3_q0[0]));
  Decoder2to4 decoder2to4_1 (
    .A1(Decoder_A0), .A0(Decoder_A1), .Y0(decoder2to4_1_y0), .Y1(decoder2to4_1_y1), .Y2(decoder2to4_1_y2),
    .Y3(decoder2to4_1_y3));
  Multiplexer #(.select(2), .width(4)) multiplexer_1 (
    .in0(R0_q0), .in1(R1_q0), .in2(R2_q0), .in3(R3_q0), .out(READ_A), .sel(READ_ADRS_A));
  Multiplexer #(.select(2), .width(4)) multiplexer_2 (
    .in0(R0_q0), .in1(R1_q0), .in2(R2_q0), .in3(R3_q0), .out(READ_B), .sel(READ_ADRS_B));
endmodule

module Datapath (
  input  Toggle,
  input  [3:0] Memory,
  input  [1:0] A_Address,
  input  [1:0] OPCODE,
  input  [1:0] B_Address,
  input  [1:0] ADRESS_WRITE_TO,
  output A3,
  output B3
);

  wire clock_1_out;
  wire [2:0] registerfile_1_read_a, registerfile_1_read_b;
  wire [3:0] alu_1_aluresult, multiplexer_1_out;

  Clock clock_1 (.out(clock_1_out));
  RegisterFile registerfile_1 (
    .D3(multiplexer_1_out[3]), .D2(multiplexer_1_out[2]), .D1(multiplexer_1_out[1]),
    .D0(multiplexer_1_out[0]), .CLOCK(clock_1_out), .READ_ADRS_A(A_Address), .READ_ADRS_B(B_Address),
    .Decoder_A0(ADRESS_WRITE_TO[0]), .Decoder_A1(ADRESS_WRITE_TO[1]), .READ_A({A3, registerfile_1_read_a}),
    .READ_B({B3, registerfile_1_read_b}));
  ALU alu_1 (
    .A({A3, registerfile_1_read_a}), .B({B3, registerfile_1_read_b}), .OPRATION(OPCODE),
    .AluResult(alu_1_aluresult));  // open: AluCout
  Multiplexer #(.width(4)) multiplexer_1 (.in0(alu_1_aluresult), .in1(Memory), .out(multiplexer_1_out), .sel(Toggle));
endmodule

module Flags (
  input  ALU_COUT,
  input  [3:0] ALU_Res,
  output C,
  output Z,
  output N,
  output V
);

  wire or_1_out, or_2_out, or_3_out;

  or or_1 (or_1_out, ALU_Res[2], ALU_Res[3]);
  or or_2 (or_2_out, ALU_Res[1], or_1_out);
  or or_3 (or_3_out, ALU_Res[0], or_2_out);
  not not_1 (Z, or_3_out);

  assign C = ALU_COUT;
  assign N = ALU_Res[3];
endmodule
